# Fritzing sketch espresso_switch (saved by Fritzing 0.9.4)
circuit board: 8.46667cm x 5.64444cm
breadboards: 1

parts:
  U1 = TLP621 [package=THT]
  R2 = Resistor [tolerance=±5% resistance=100 package="0805 [SMD]"]
  U2 = RELAY-SOLIDSTATE [package=relay-s108t02]
  R4 = Resistor [tolerance=±5% resistance=100 package="0805 [SMD]"]
  R5 = Resistor [tolerance=±5% resistance=100 package="0805 [SMD]"]
  S1 = Pushbutton [package="[SMD]"]
  JP2 = Header 2 [package=molex-1x2_lock]
  HLK-PM1 = HLK-PM01
  JP3 = Header 2 [package=molex-1x2_lock]
  LED1 = LED - 3mm [color="Red (633nm)" package="3 mm [THT]"]
  JP1 = Header 2 [package=molex-1x2_lock]
  D1 = Rectifier Diode [part_number=1N4001 package="300 mil [THT]"]
  WeMos_D1_Mini1 = WeMos D1 Mini

nets (from the breadboard view):
  N1: U1.Pin_1, JP2.1
  N2: U1.Pin_2, R2.Pin_0
  N3: U1.Pin_4, R4.Pin_1, R5.Pin_1, S1.Pin_1, S1.Pin_2, HLK-PM1.-Vo, D1.anode, WeMos_D1_Mini1.G
  N4: U1.Pin_3, WeMos_D1_Mini1.D6
  N5: R2.Pin_1, JP2.2
  N6: U2.T1, JP1.1
  N7: U2.T2, JP1.2
  N8: U2.+, D1.cathode, WeMos_D1_Mini1.D5
  N9: U2.-, R4.Pin_0
  N10: R5.Pin_0, LED1.anode
  N11: S1.Pin_3, S1.Pin_4, WeMos_D1_Mini1.D2
  N12: HLK-PM1.AC#0, JP3.1
  N13: HLK-PM1.AC#1, JP3.2
  N14: HLK-PM1.+Vo, WeMos_D1_Mini1.5V
  N15: LED1.cathode, WeMos_D1_Mini1.D4

notes:
  Power Sense (D6) - power sense with optocoupler. Pullup configuration
  button (D2) - reset settings button, hold 10s to activate and reset wifi & homekit, press to toggle espresso power. Pullup configuration
  Relay (D5) - output for the espresso momentary switch circuit
  LED (D4) - indicates the status of the device
  J3 AC Mains
  J2 Relay
  J1 Power Sense
